# Fritzing sketch RZD Controller sheme (saved by Fritzing 0.9.5d)

parts:
  Gizwits_WiFi_Witty_ESP-12F1 = Gizwits WiFi Witty ESP-12F
  L298N1 = L298N DC motor driver
  Yumo-enc1 = YumoE6B2
  M1 = DC Motor  # not connected
  Bat1 = battery_holder_single_18650
  S1 = Round Pushbutton

nets:
  N1: Gizwits_WiFi_Witty_ESP-12F1.GPIO14, L298N1.ENB
  N2: Gizwits_WiFi_Witty_ESP-12F1.GPIO12, L298N1.IN4
  N3: Gizwits_WiFi_Witty_ESP-12F1.GPIO13, L298N1.IN3
  N4: Gizwits_WiFi_Witty_ESP-12F1.GPIO15, Yumo-enc1.Z
  N5: Gizwits_WiFi_Witty_ESP-12F1.GPIO2, Yumo-enc1.B
  N6: Gizwits_WiFi_Witty_ESP-12F1.GPIO0, Yumo-enc1.A
  N7: Bat1.+#0, S1.leg0

custom parts:
  L298N DC motor driver: 2x DC motor driver with 78M05 positive voltage regulator (7..35 V) L298N: max 46 V, 2 A Set 5 V Enable jumper to enable 5 V regultor (needed for the L298N) and +5 V output at screw terminal or supply external +5 V at screw terminal Set ENA and/or ENB to +5 V to enable motor permanently or supply ENA and/or ENB with PWM signal IN1 and IN2 set rotation directory for motor A (OUT1/OUT2) IN2 and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
  battery_holder_single_18650: single 18650 battery holder
