# Fritzing sketch Драйвер моторов (saved by Fritzing 0.9.5d)

parts:
  Part1 = Adafruit PCA9685 PWM/Servo Breakout [part_number=815]
  Part2 = Motor Driver 1A Dual TB6612FNG
  Part3 = Motor Driver 1A Dual TB6612FNG
  J1 = kf301-5.0-2p [package=THT]  # not connected
  IC1 = IC, DIP package, 8 pins [chip_label=IC]
  IC2 = IC, DIP package, 8 pins [chip_label=IC]
  C1 = Electrolytic Capacitor [capacitance=100µF voltage=16V package="100 mil [THT, electrolytic]"]
  J2 = Dagu DGServo 9g header (male) [package=THT]
  J3 = Dagu DGServo 9g header (male) [package=THT]
  J4 = Dagu DGServo 9g header (male) [package=THT]
  J5 = Dagu DGServo 9g header (male) [package=THT]
  J6 = kf301-5.0-2p [package=THT]
  J7 = kf301-5.0-2p [package=THT]  # not connected
  J8 = kf301-5.0-2p [package=THT]  # not connected
  J9 = kf301-5.0-2p [package=THT]  # not connected
  J10 = kf301-5.0-2p [package=THT]  # not connected
  J11 = kf301-5.0-2p [package=THT]  # not connected

nets:
  N1: Part1.PWM7, IC1.pin2
  N2: Part1.5.0V, Part3.VCC
  GND: Part1.GND, Part3.GND
  N3: Part1.PWM6, IC1.pin1
  N4: Part1.PWM5, IC2.pin2
  N5: Part1.PWM4, IC2.pin1
  N6: Part1.PWM3, Part3.BIN2
  N7: Part1.PWM2, Part3.BIN1
  N8: Part1.PWM1, Part3.AIN1
  N9: Part1.PWM0, Part3.AIN2
  N10: Part1.PWM15, J4.gnd
  N11: Part1.PWM14, J2.gnd
  N12: Part1.PWM13, J3.gnd
  N13: Part1.PWM12, J5.gnd
  N14: Part1.PWM11, Part2.BIN2
  N15: Part1.PWM10, Part2.BIN1
  N16: Part1.PWM9, Part2.AIN1
  N17: Part1.PWM8, Part2.AIN2
  N18: Part2.VM, C1.+
  N19: Part3.VM, J6.pin1
  N20: IC1.pin5, IC1.pin6
  N21: IC1.pin7, IC1.pin8
  N22: IC2.pin5, IC2.pin6
  N23: IC2.pin7, IC2.pin8
  VCC: J2.Vcc, J3.Vcc, J4.Vcc, J5.Vcc
  N24: J2.pulse, J3.pulse, J4.pulse, J5.pulse

custom parts:
  Adafruit PCA9685 PWM/Servo Breakout: Using only two pins, control 16 free-running PWM outputs! I2C-controlled PWM driver with a built in clock. Unlike the TLC5940 family, you do not need to continuously send it signal tying up your microcontroller, its completely free running! 5V compliant, which means you can control it from a 3.3V microcontroller and still safely drive up to 6V outputs (this is good for when you want to control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
  kf301-5.0-2p: Screw terminal with 5mm pins
