# Fritzing sketch Разьем датчика расстояния (saved by Fritzing 0.9.5d)

parts:
  Part1 = Ethernet Cable
  X1 = DB9 Connector Male [package=db9]

nets:
  N1: Part1.pin_1, Part1.pin_5, X1.1, X1.2
  N2: Part1.pin_2, X1.6
  N3: Part1.pin_3, X1.7
  N4: Part1.pin_4, Part1.pin_7, X1.4, X1.5
  N5: Part1.pin_6, X1.8
  N6: Part1.pin_8, X1.9

notes:
  VCC
  GND
  SCL
  SDA

custom parts:
  DB9 Connector Male: DB9 Connector Standard DB9 (D-Sub 9) serial connector. Can be used for CAN bus as well as RS485 and RS232. Footprint production proven. Spark Fun Electronics SKU : PRT-00429
