# Fritzing sketch Разьем сервоприводов (saved by Fritzing 0.9.5d)

parts:
  Part2 = Ethernet Cable
  X2 = DB9 Connector Male [package=db9]

nets:
  N1: Part2.pin_1, Part2.pin_2, X2.1, X2.2
  N2: Part2.pin_3, X2.6
  N3: Part2.pin_4, Part2.pin_7, X2.4, X2.5
  N4: Part2.pin_8, X2.9

notes:
  VCC
  GND
  PWM

custom parts:
  DB9 Connector Male: DB9 Connector Standard DB9 (D-Sub 9) serial connector. Can be used for CAN bus as well as RS485 and RS232. Footprint production proven. Spark Fun Electronics SKU : PRT-00429
